# Fritzing sketch ESP32 (saved by Fritzing 0.9.8b)
breadboards: 1

parts:
  HUB75 = shrouded pin header, 16 pins [form="♂ (shrouded male)"]
  U1 = ESP32-HiLetgo [part_number=ESP32S-HiLetgo]

nets:
  N1: HUB75.pin1, U1.connector8
  N2: HUB75.pin2, U1.connector10
  N3: HUB75.pin3, U1.connector11
  N4: HUB75.pin4, U1.connector14
  N5: HUB75.pin5, U1.connector36
  N6: HUB75.pin6, U1.connector28
  N7: HUB75.pin7, U1.connector26
  N8: HUB75.pin8, U1.connector22
  GND: HUB75.pin9, HUB75.pin15, U1.connector37
  N9: HUB75.pin10, U1.connector25
  N10: HUB75.pin11, U1.connector27
  N11: HUB75.pin12, U1.connector30
  N12: HUB75.pin14, U1.connector12
  N13: HUB75.pin16, U1.connector9
  5V: U1.connector18
